# Fritzing sketch color-calc-cirquit (saved by Fritzing 0.9.3b)
circuit board: 8.46667cm x 5.64444cm
breadboards: 1

parts:
  S1 = SWITCH-MOMENTARY-2 [package=tactile_switch_tall]
  S2 = SWITCH-MOMENTARY-2 [package=tactile_switch_tall]
  S3 = SWITCH-MOMENTARY-2 [package=tactile_switch_tall]
  S4 = SWITCH-MOMENTARY-2 [package=tactile_switch_tall]
  S5 = SWITCH-MOMENTARY-2 [package=tactile_switch_tall]
  S6 = SWITCH-MOMENTARY-2 [package=tactile_switch_tall]
  S7 = SWITCH-MOMENTARY-2 [package=tactile_switch_tall]
  S8 = SWITCH-MOMENTARY-2 [package=tactile_switch_tall]
  S9 = SWITCH-MOMENTARY-2 [package=tactile_switch_tall]
  S10 = SWITCH-MOMENTARY-2 [package=tactile_switch_tall]
  S11 = SWITCH-MOMENTARY-2 [package=tactile_switch_tall]
  S12 = SWITCH-MOMENTARY-2 [package=tactile_switch_tall]
  S13 = SWITCH-MOMENTARY-2 [package=tactile_switch_tall]
  S14 = SWITCH-MOMENTARY-2 [package=tactile_switch_tall]
  S15 = SWITCH-MOMENTARY-2 [package=tactile_switch_tall]
  S16 = SWITCH-MOMENTARY-2 [package=tactile_switch_tall]
  LED1 = RGB LED (com. cathode, rbg) [package="5 mm [THT]"]
  R1 = Resistor [tolerance=±5% resistance=640 package="2512 [SMD]"]
  R2 = Resistor [tolerance=±5% resistance=640 package="2512 [SMD]"]
  R3 = Resistor [tolerance=±5% resistance=640 package="2512 [SMD]"]
  LED2 = RGB LED (com. cathode, rbg) [package="5 mm [THT]"]
  R4 = Resistor [tolerance=±5% resistance=640 package="2512 [SMD]"]
  R5 = Resistor [tolerance=±5% resistance=640 package="2512 [SMD]"]
  R6 = Resistor [tolerance=±5% resistance=640 package="2512 [SMD]"]
  LED3 = RGB LED (com. cathode, rbg) [package="5 mm [THT]"]
  R7 = Resistor [tolerance=±5% resistance=640 package="2512 [SMD]"]
  R8 = Resistor [tolerance=±5% resistance=640 package="2512 [SMD]"]
  R9 = Resistor [tolerance=±5% resistance=640 package="2512 [SMD]"]
  V1 = DC Power [voltage=4.5V]
  S17 = SWITCH-MOMENTARY-2 [package=tactile-switch-1101ne]
  Part1 = Arduino Pro Mini v13

nets:
  N1: S1.2, S2.2, S3.2, S4.2, Part1.D13/SCK
  N2: S1.1, S6.1, S10.1, S14.1, Part1.A0
  N3: S2.1, S8.1, S12.1, S16.1, Part1.A1
  N4: S3.1, S5.1, S9.1, S13.1, Part1.A2
  N5: S4.1, S7.1, S11.1, S15.1, Part1.A3
  N6: S5.2, S6.2, S7.2, S8.2, Part1.D12/MISO
  N7: S9.2, S10.2, S11.2, S12.2, Part1.D11_PWM/MOSI
  N8: S13.2, S14.2, S15.2, S16.2, Part1.D10_PWM/SS
  N9: LED1.red_anode, R1.Pin_0
  GND: LED1.common_cathode, LED2.common_cathode, LED3.common_cathode, V1.V-, Part1.GND
  N10: LED1.blue_anode, R2.Pin_0
  N11: LED1.green_anode, R3.Pin_0
  N12: R1.Pin_1, R6.Pin_1, R9.Pin_1, Part1.D3_PWM
  N13: R2.Pin_1, R5.Pin_1, R8.Pin_1, Part1.D6_PWM
  N14: R3.Pin_1, R4.Pin_1, R7.Pin_1, Part1.D5_PWM
  N15: LED2.red_anode, R6.Pin_0
  N16: LED2.blue_anode, R5.Pin_0
  N17: LED2.green_anode, R4.Pin_0
  N18: LED3.red_anode, R9.Pin_0
  N19: LED3.blue_anode, R8.Pin_0
  N20: LED3.green_anode, R7.Pin_0
  N21: V1.V+, S17.1
  N22: S17.2, Part1.RAW
